// Logisim project Addition & Subtraction.circ as structural Verilog: 12 circuits, main circuit Subtraction
module adder (
  input  Previous_Carry,
  input  [4:0] A,
  input  [4:0] B,
  output [4:0] OutPut,
  output Carry
);

  wire full_adder_1_c, full_adder_2_c, full_adder_3_c, full_adder_4_c;

  full_adder full_adder_1 (.A(A[0]), .B(B[0]), .Co(Previous_Carry), .sum(OutPut[0]), .C(full_adder_1_c));
  full_adder full_adder_2 (.A(A[1]), .B(B[1]), .Co(full_adder_1_c), .sum(OutPut[1]), .C(full_adder_2_c));
  full_adder full_adder_3 (.A(A[2]), .B(B[2]), .Co(full_adder_2_c), .sum(OutPut[2]), .C(full_adder_3_c));
  full_adder full_adder_4 (.A(A[3]), .B(B[3]), .Co(full_adder_3_c), .sum(OutPut[3]), .C(full_adder_4_c));
  full_adder full_adder_5 (.A(A[4]), .B(B[4]), .Co(full_adder_4_c), .sum(OutPut[4]), .C(Carry));
endmodule

module full_adder (
  input  A,
  input  B,
  input  Co,
  output sum,
  output C
);

  wire and_1_out, and_2_out, xor_1_out;

  xor xor_1 (xor_1_out, A, B);
  and and_1 (and_1_out, A, B);
  xor xor_2 (sum, xor_1_out, Co);
  and and_2 (and_2_out, xor_1_out, Co);
  or or_1 (C, and_2_out, and_1_out);
endmodule

module _6_bit_1complement (
  input  [5:0] InPut_A,
  output [5:0] OutPut
);

  wire not_1_out;

  not not_1 (not_1_out, 1'b0);
  xor xor_1 (OutPut[4], InPut_A[4], not_1_out);
  xor xor_2 (OutPut[3], InPut_A[3], not_1_out);
  xor xor_3 (OutPut[5], InPut_A[5], not_1_out);
  xor xor_4 (OutPut[1], InPut_A[1], not_1_out);
  xor xor_5 (OutPut[2], InPut_A[2], not_1_out);
  xor xor_6 (OutPut[0], InPut_A[0], not_1_out);
endmodule

module _6_bits_adder (
  input  Carry,
  input  [5:0] InPut_A,
  output [5:0] OutPut
);

  wire full_adder_2_c, full_adder_3_c, full_adder_4_c, full_adder_5_c, full_adder_6_c, full_adder_c,
       not_1_out;

  not not_1 (not_1_out, 1'b0);
  full_adder full_adder (.A(InPut_A[0]), .B(not_1_out), .Co(Carry), .sum(OutPut[0]), .C(full_adder_c));
  full_adder full_adder_2 (.A(InPut_A[1]), .B(1'b0), .Co(full_adder_c), .sum(OutPut[1]), .C(full_adder_2_c));
  full_adder full_adder_3 (.A(InPut_A[2]), .B(1'b0), .Co(full_adder_2_c), .sum(OutPut[2]), .C(full_adder_3_c));
  full_adder full_adder_4 (.A(InPut_A[3]), .B(1'b0), .Co(full_adder_3_c), .sum(OutPut[3]), .C(full_adder_4_c));
  full_adder full_adder_5 (.A(InPut_A[4]), .B(1'b0), .Co(full_adder_4_c), .sum(OutPut[4]), .C(full_adder_5_c));
  full_adder full_adder_6 (.A(InPut_A[5]), .B(1'b0), .Co(full_adder_5_c), .sum(OutPut[5]), .C(full_adder_6_c));
endmodule

module compare (
  input  [4:0] InPut_A,
  input  [4:0] InPut_B,
  output [5:0] OutPut
);

  wire adder_p5, not_1_out, xor_1_out;
  wire [4:4] adder_p4;

  // addllllllllllllllllllllllllllsub_adder adder: pin names not known; wires that end beside it: InPut_A, InPut_B, 1'b0, {adder_p4[4], OutPut[3:0]}, adder_p5
  not not_1 (not_1_out, adder_p5);
  xor xor_1 (xor_1_out, InPut_A[4], InPut_B[4]);
  // addllllllllllllllllllllllllllsub_multiplexier multiplexier: pin names not known; wires that end beside it: adder_p4[4], xor_1_out, OutPut[4], not_1_out
  // addllllllllllllllllllllllllllsub_multiplexier multiplexier_2: pin names not known; wires that end beside it: adder_p5, xor_1_out, OutPut[5], adder_p4[4]
endmodule

module fromsignto2_s (
  input  [4:0] InPut,
  output [4:0] OutPut
);

  wire not_1_out, not_2_out;
  wire [3:0] xor_4_out;
  wire [4:0] adder_output;

  not not_1 (not_1_out, 1'b0);
  xor xor_1 (xor_4_out[3], not_1_out, InPut[3]);
  xor xor_2 (xor_4_out[2], not_1_out, InPut[2]);
  xor xor_3 (xor_4_out[1], not_1_out, InPut[1]);
  xor xor_4 (xor_4_out[0], not_1_out, InPut[0]);
  not not_2 (not_2_out, 1'b0);
  adder adder (
    .A({InPut[4], xor_4_out}), .B({5{1'b0}}), .Previous_Carry(not_2_out), .OutPut(adder_output));  // open: Carry
  _5bits_multiplixier _5bits_multiplixier (
    .InPut_A0(adder_output), .InPut_s1(InPut[4]), .InPut_A1(InPut), .OutPut(OutPut));
endmodule

module multiplexier (
  input  InPut_A0,
  input  InPut_S1,
  input  InPut_A1,
  output OutPut
);

  wire nand_1_out, nand_2_out, nand_3_out;

  nand nand_1 (nand_1_out, InPut_A0, InPut_S1);
  nand nand_2 (nand_2_out, InPut_S1, InPut_S1);
  nand nand_3 (nand_3_out, nand_2_out, InPut_A1);
  nand nand_4 (OutPut, nand_1_out, nand_3_out);
endmodule

module _5bits_multiplixier (
  input  [4:0] InPut_A0,
  input  InPut_s1,
  input  [4:0] InPut_A1,
  output [4:0] OutPut
);

  multiplexier multiplexier (.InPut_A0(InPut_A0[4]), .InPut_S1(InPut_s1), .InPut_A1(InPut_A1[4]), .OutPut(OutPut[4]));
  multiplexier multiplexier_2 (.InPut_A0(InPut_A0[3]), .InPut_S1(InPut_s1), .InPut_A1(InPut_A1[3]), .OutPut(OutPut[3]));
  multiplexier multiplexier_3 (.InPut_A0(InPut_A0[2]), .InPut_S1(InPut_s1), .InPut_A1(InPut_A1[2]), .OutPut(OutPut[2]));
  multiplexier multiplexier_4 (.InPut_A0(InPut_A0[1]), .InPut_S1(InPut_s1), .InPut_A1(InPut_A1[1]), .OutPut(OutPut[1]));
  multiplexier multiplexier_5 (.InPut_A0(InPut_A0[0]), .InPut_S1(InPut_s1), .InPut_A1(InPut_A1[0]), .OutPut(OutPut[0]));
endmodule

module _6bits_multiplxier (
  input  [5:0] InPut_A0,
  input  s1,
  input  [5:0] InPut_A1,
  output [5:0] OutPut
);

  multiplexier multiplexier (.InPut_A0(InPut_A0[5]), .InPut_S1(s1), .InPut_A1(InPut_A1[5]), .OutPut(OutPut[5]));
  multiplexier multiplexier_2 (.InPut_A0(InPut_A0[4]), .InPut_S1(s1), .InPut_A1(InPut_A1[4]), .OutPut(OutPut[4]));
  multiplexier multiplexier_3 (.InPut_A0(InPut_A0[3]), .InPut_S1(s1), .InPut_A1(InPut_A1[3]), .OutPut(OutPut[3]));
  multiplexier multiplexier_4 (.InPut_A0(InPut_A0[2]), .InPut_S1(s1), .InPut_A1(InPut_A1[2]), .OutPut(OutPut[2]));
  multiplexier multiplexier_5 (.InPut_A0(InPut_A0[1]), .InPut_S1(s1), .InPut_A1(InPut_A1[1]), .OutPut(OutPut[1]));
  multiplexier multiplexier_6 (.InPut_A0(InPut_A0[0]), .InPut_S1(s1), .InPut_A1(InPut_A1[0]), .OutPut(OutPut[0]));
endmodule

module Subtraction (
  input  [4:0] InPut_A,
  input  [4:0] InPut_B,
  output [7:0] Subtraction,
  output Sign
);

  wire [4:0] _5bits_2_s_comp_output, Comparator___Adder_output, Converter_2_output, Converter_output;
  wire [5:0] _6_bit_1complement_output, _6_bits_adder_output;

  fromsignto2_s Converter (.InPut(InPut_A), .OutPut(Converter_output));
  fromsignto2_s Converter_2 (.InPut(InPut_B), .OutPut(Converter_2_output));
  _5bits_2omp _5bits_2_s_comp (.InPut_A(Converter_2_output), .OutPut(_5bits_2_s_comp_output));
  compare Comparator___Adder (
    .InPut_A(Converter_output), .InPut_B(_5bits_2_s_comp_output), .OutPut({Sign, Comparator___Adder_output}));
  _6_bit_1complement _6_bit_1complement (
    .InPut_A({Sign, Comparator___Adder_output}), .OutPut(_6_bit_1complement_output));
  _6_bits_adder _6_bits_adder (.InPut_A(_6_bit_1complement_output), .Carry(1'b0), .OutPut(_6_bits_adder_output));
  _6bits_multiplxier _6bits_multiplxier (
    .InPut_A0(_6_bits_adder_output), .s1(Sign), .InPut_A1({Sign, Comparator___Adder_output}),
    .OutPut(Subtraction[5:0]));

  assign Subtraction[7:6] = 2'b00;
endmodule

module _5bits_2omp (
  input  [4:0] InPut_A,
  output [4:0] OutPut
);

  wire not_1_out;
  wire [4:0] xor_4_out;

  not not_1 (not_1_out, 1'b0);
  xor xor_1 (xor_4_out[2], InPut_A[2], not_1_out);
  xor xor_2 (xor_4_out[3], InPut_A[3], not_1_out);
  xor xor_3 (xor_4_out[4], InPut_A[4], not_1_out);
  xor xor_4 (xor_4_out[0], InPut_A[0], not_1_out);
  xor xor_5 (xor_4_out[1], InPut_A[1], not_1_out);
  adder adder (.A(xor_4_out), .B({5{1'b0}}), .Previous_Carry(not_1_out), .OutPut(OutPut));  // open: Carry
endmodule

module Addition (
  input  [4:0] A,
  input  [4:0] B,
  output [7:0] Summation,
  output Sign
);

  wire [4:0] Comparator___Adder_output, Converter_2_output, Converter_output;
  wire [5:0] _6_bit_1complement_output, _6_bits_adder_output;

  fromsignto2_s Converter (.InPut(A), .OutPut(Converter_output));
  fromsignto2_s Converter_2 (.InPut(B), .OutPut(Converter_2_output));
  compare Comparator___Adder (
    .InPut_A(Converter_output), .InPut_B(Converter_2_output), .OutPut({Sign, Comparator___Adder_output}));
  _6_bit_1complement _6_bit_1complement (
    .InPut_A({Sign, Comparator___Adder_output}), .OutPut(_6_bit_1complement_output));
  _6_bits_adder _6_bits_adder (.InPut_A(_6_bit_1complement_output), .Carry(1'b0), .OutPut(_6_bits_adder_output));
  _6bits_multiplxier _6bits_multiplxier (
    .InPut_A0(_6_bits_adder_output), .s1(Sign), .InPut_A1({Sign, Comparator___Adder_output}),
    .OutPut(Summation[5:0]));

  assign Summation[7:6] = 2'b00;
endmodule
