// Logisim project Division & BCD to 7 segments.circ as structural Verilog: 17 circuits, main circuit Division
module _4_Bit_Divider (
  input  [3:0] A,
  input  [3:0] B,
  output Q1,
  output Q2,
  output Q3,
  output Q4
);

  wire [3:0] n4_bit_subtractor_1_result, n4_bit_subtractor_2_result, n4_bit_subtractor_3_result,
       q_b_1_result, q_b_2_result, q_b_3_result;

  _4_Bit_Comparator u_4_bit_comparator_1 (
    .Ao(A[3]), .A1(1'b0), .A2(1'b0), .A3(1'b0), .Bo(B[0]), .B1(B[1]), .B2(B[2]), .B3(B[3]), .A__B(Q1));
  Q___B q_b_1 (.Q(Q1), .B(B), .Result(q_b_1_result));
  _4_Bit_Subtractor u_4_bit_subtractor_1 (.A({3'b000, A[3]}), .B(q_b_1_result), .Result(n4_bit_subtractor_1_result));
  _4_Bit_Comparator u_4_bit_comparator_2 (
    .Ao(A[2]), .A1(n4_bit_subtractor_1_result[0]), .A2(n4_bit_subtractor_1_result[1]),
    .A3(n4_bit_subtractor_1_result[2]), .Bo(B[0]), .B1(B[1]), .B2(B[2]), .B3(B[3]), .A__B(Q2));
  Q___B q_b_2 (.Q(Q2), .B(B), .Result(q_b_2_result));
  _4_Bit_Subtractor u_4_bit_subtractor_2 (
    .A({n4_bit_subtractor_1_result[2:0], A[2]}), .B(q_b_2_result), .Result(n4_bit_subtractor_2_result));
  _4_Bit_Comparator u_4_bit_comparator_3 (
    .Ao(A[1]), .A1(n4_bit_subtractor_2_result[0]), .A2(n4_bit_subtractor_2_result[1]),
    .A3(n4_bit_subtractor_2_result[2]), .Bo(B[0]), .B1(B[1]), .B2(B[2]), .B3(B[3]), .A__B(Q3));
  Q___B q_b_3 (.Q(Q3), .B(B), .Result(q_b_3_result));
  _4_Bit_Subtractor u_4_bit_subtractor_3 (
    .A({n4_bit_subtractor_2_result[2:0], A[1]}), .B(q_b_3_result), .Result(n4_bit_subtractor_3_result));
  _4_Bit_Comparator u_4_bit_comparator_4 (
    .Ao(A[0]), .A1(n4_bit_subtractor_3_result[0]), .A2(n4_bit_subtractor_3_result[1]),
    .A3(n4_bit_subtractor_3_result[2]), .Bo(B[0]), .B1(B[1]), .B2(B[2]), .B3(B[3]), .A__B(Q4));
endmodule

// HA
module Half_Adder (
  input  x,
  input  y,
  output SUM,
  output CARRY
);

  xor XOR (SUM, x, y);
  and AND (CARRY, x, y);
endmodule

// FA
module Full_Adder (
  input  x,
  input  y,
  input  z,
  output SUM,
  output CARRY
);

  wire half_adder_1_carry, half_adder_1_sum, half_adder_2_carry;

  Half_Adder half_adder_1 (.x(x), .y(y), .SUM(half_adder_1_sum), .CARRY(half_adder_1_carry));
  Half_Adder half_adder_2 (.x(half_adder_1_sum), .y(z), .SUM(SUM), .CARRY(half_adder_2_carry));
  or OR (CARRY, half_adder_2_carry, half_adder_1_carry);
endmodule

module BCD_to_7Segments (
  input  _1,
  input  _2,
  input  _3,
  input  _4,
  output a,
  output b,
  output c,
  output d,
  output e,
  output f,
  output g
);

  abcdefg abcdefg_1 (.in_1(_4), .in_2(_3), .in_3(_2), .in_4(_1), .a(a), .b(b), .c(c), .d(d), .e(e), .f(f), .g(g));
endmodule

module a (
  input  A,
  input  B,
  input  C,
  input  D,
  output a_2
);

  wire and_1_out, and_2_out, and_3_out, and_4_out, and_5_out, and_6_out, and_7_out, not_1_out, not_2_out,
       not_3_out, not_4_out, not_5_out, not_6_out, or_1_out, or_2_out;

  not not_1 (not_1_out, A);
  not not_2 (not_2_out, B);
  not not_3 (not_3_out, C);
  not not_4 (not_4_out, D);
  not not_5 (not_5_out, B);
  not not_6 (not_6_out, C);
  and and_1 (and_1_out, not_1_out, B);
  and and_2 (and_2_out, not_2_out, not_3_out);
  and and_3 (and_3_out, not_1_out, C);
  and and_4 (and_4_out, A, not_5_out);
  and and_5 (and_5_out, and_1_out, D);
  and and_6 (and_6_out, and_2_out, not_4_out);
  and and_7 (and_7_out, and_4_out, not_6_out);
  or or_1 (or_1_out, and_3_out, and_5_out);
  or or_2 (or_2_out, and_6_out, and_7_out);
  or or_3 (a_2, or_1_out, or_2_out);
endmodule

module b (
  input  A,
  input  B,
  input  C,
  input  D,
  output b_2
);

  wire and_1_out, and_2_out, and_3_out, and_4_out, and_5_out, and_6_out, and_7_out, not_1_out, not_2_out,
       not_3_out, not_4_out, or_1_out, or_2_out;

  not not_1 (not_1_out, A);
  not not_2 (not_2_out, B);
  not not_3 (not_3_out, C);
  not not_4 (not_4_out, D);
  and and_1 (and_1_out, not_1_out, not_2_out);
  and and_2 (and_2_out, not_1_out, not_3_out);
  and and_3 (and_3_out, not_1_out, C);
  and and_4 (and_4_out, A, not_2_out);
  and and_5 (and_5_out, and_2_out, not_4_out);
  and and_6 (and_6_out, and_3_out, D);
  and and_7 (and_7_out, and_4_out, not_3_out);
  or or_1 (or_1_out, and_1_out, and_5_out);
  or or_2 (or_2_out, and_6_out, and_7_out);
  or or_3 (b_2, or_1_out, or_2_out);
endmodule

module c (
  input  A,
  input  B,
  input  C,
  input  D,
  output c_2
);

  wire and_1_out, and_2_out, and_3_out, and_4_out, and_5_out, and_6_out, not_1_out, not_2_out, not_3_out,
       not_4_out, not_5_out, not_6_out, not_7_out, or_1_out, or_2_out;

  not not_1 (not_1_out, A);
  not not_2 (not_2_out, A);
  not not_3 (not_3_out, B);
  not not_4 (not_4_out, C);
  not not_5 (not_5_out, D);
  not not_6 (not_6_out, B);
  not not_7 (not_7_out, C);
  and and_1 (and_1_out, not_3_out, not_4_out);
  and and_2 (and_2_out, A, not_6_out);
  and and_3 (and_3_out, not_1_out, B);
  and and_4 (and_4_out, not_2_out, D);
  and and_5 (and_5_out, and_1_out, not_5_out);
  and and_6 (and_6_out, and_2_out, not_7_out);
  or or_1 (or_1_out, and_3_out, and_4_out);
  or or_2 (or_2_out, and_5_out, and_6_out);
  or or_3 (c_2, or_1_out, or_2_out);
endmodule

module d (
  input  A,
  input  B,
  input  C,
  input  D,
  output d_2
);

  wire and_1_out, and_2_out, and_3_out, and_4_out, and_5_out, and_6_out, and_7_out, and_8_out, and_9_out,
       and_10_out, and_11_out, not_1_out, not_2_out, not_3_out, not_4_out, not_5_out, or_1_out, or_2_out,
       or_3_out;

  not not_1 (not_1_out, A);
  not not_2 (not_2_out, D);
  not not_3 (not_3_out, B);
  not not_4 (not_4_out, C);
  not not_5 (not_5_out, D);
  and and_1 (and_1_out, not_1_out, B);
  and and_2 (and_2_out, D, not_4_out);
  and and_3 (and_3_out, not_1_out, C);
  and and_4 (and_4_out, not_1_out, not_3_out);
  and and_5 (and_5_out, not_3_out, not_4_out);
  and and_6 (and_6_out, A, not_3_out);
  and and_7 (and_7_out, and_1_out, and_2_out);
  and and_8 (and_8_out, and_3_out, not_2_out);
  and and_9 (and_9_out, and_4_out, C);
  and and_10 (and_10_out, and_5_out, not_5_out);
  and and_11 (and_11_out, and_6_out, not_4_out);
  or or_1 (or_1_out, and_7_out, and_8_out);
  or or_2 (or_2_out, and_9_out, and_10_out);
  or or_3 (or_3_out, or_2_out, and_11_out);
  or or_4 (d_2, or_1_out, or_3_out);
endmodule

module e (
  input  A,
  input  B,
  input  C,
  input  D,
  output e
);

  wire and_1_out, and_2_out, and_3_out, and_4_out, not_1_out, not_2_out, not_3_out, not_4_out;

  not not_1 (not_1_out, A);
  not not_2 (not_2_out, D);
  not not_3 (not_3_out, B);
  not not_4 (not_4_out, C);
  and and_1 (and_1_out, not_1_out, C);
  and and_2 (and_2_out, and_1_out, not_2_out);
  and and_3 (and_3_out, not_3_out, not_2_out);
  and and_4 (and_4_out, and_3_out, not_4_out);
  or or_1 (e, and_2_out, and_4_out);
endmodule

module f (
  input  A,
  input  B,
  input  C,
  input  D,
  output f
);

  wire and_1_out, and_2_out, and_3_out, and_4_out, and_5_out, and_6_out, and_7_out, and_8_out, not_1_out,
       not_2_out, not_3_out, not_4_out, or_1_out, or_2_out;

  not not_1 (not_1_out, A);
  not not_2 (not_2_out, C);
  not not_3 (not_3_out, D);
  and and_1 (and_1_out, not_1_out, B);
  and and_2 (and_2_out, not_1_out, not_2_out);
  and and_3 (and_3_out, not_1_out, B);
  and and_4 (and_4_out, A, not_4_out);
  not not_4 (not_4_out, B);
  and and_5 (and_5_out, and_1_out, not_2_out);
  and and_6 (and_6_out, and_2_out, not_3_out);
  and and_7 (and_7_out, and_3_out, not_3_out);
  and and_8 (and_8_out, and_4_out, not_2_out);
  or or_1 (or_1_out, and_5_out, and_6_out);
  or or_2 (or_2_out, and_7_out, and_8_out);
  or or_3 (f, or_1_out, or_2_out);
endmodule

module g (
  input  A,
  input  B,
  input  C,
  input  D,
  output g
);

  wire and_1_out, and_2_out, and_3_out, and_4_out, and_5_out, and_6_out, and_7_out, and_8_out, not_1_out,
       not_2_out, not_3_out, not_4_out, or_1_out, or_2_out;

  not not_1 (not_1_out, A);
  not not_2 (not_2_out, D);
  not not_3 (not_3_out, B);
  not not_4 (not_4_out, C);
  and and_1 (and_1_out, not_1_out, C);
  and and_2 (and_2_out, not_1_out, not_3_out);
  and and_3 (and_3_out, not_1_out, B);
  and and_4 (and_4_out, A, not_3_out);
  and and_5 (and_5_out, and_1_out, not_2_out);
  and and_6 (and_6_out, and_2_out, C);
  and and_7 (and_7_out, and_3_out, not_4_out);
  and and_8 (and_8_out, and_4_out, not_4_out);
  or or_1 (or_1_out, and_5_out, and_6_out);
  or or_2 (or_2_out, and_7_out, and_8_out);
  or or_3 (g, or_1_out, or_2_out);
endmodule

module abcdefg (
  input  in_1,
  input  in_2,
  input  in_3,
  input  in_4,
  output a,
  output b,
  output c,
  output d,
  output e,
  output f,
  output g
);

  a u_a (.A(in_1), .B(in_2), .C(in_3), .D(in_4), .a_2(a));
  b u_b (.A(in_1), .B(in_2), .C(in_3), .D(in_4), .b_2(b));
  c u_c (.A(in_1), .B(in_2), .C(in_3), .D(in_4), .c_2(c));
  d u_d (.A(in_1), .B(in_2), .C(in_3), .D(in_4), .d_2(d));
  e u_e (.A(in_1), .B(in_2), .C(in_3), .D(in_4), .e(e));
  f u_f (.A(in_1), .B(in_2), .C(in_3), .D(in_4), .f(f));
  g u_g (.A(in_1), .B(in_2), .C(in_3), .D(in_4), .g(g));
endmodule

module _1_Bit_Comparator (
  input  A,
  input  B,
  output E__A___B,
  output S__A___B
);

  wire and_1_out, not_1_out, not_2_out, or_1_out;

  not not_1 (not_1_out, A);
  not not_2 (not_2_out, B);
  and and_1 (and_1_out, not_1_out, B);
  and and_2 (S__A___B, not_2_out, A);
  or or_1 (or_1_out, and_1_out, S__A___B);
  not not_3 (E__A___B, or_1_out);
endmodule

// Comp
module _4_Bit_Comparator (
  input  Ao,
  input  A1,
  input  A2,
  input  A3,
  input  Bo,
  input  B1,
  input  B2,
  input  B3,
  output A__B
);

  wire _1_Bit_Comparator_2_e__a___b, _1_Bit_Comparator_2_s__a___b, _1_Bit_Comparator_3_e__a___b,
       _1_Bit_Comparator_3_s__a___b, _1_Bit_Comparator_4_e__a___b, _1_Bit_Comparator_4_s__a___b,
       _1_Bit_Comparator_e__a___b, _1_Bit_Comparator_s__a___b, and_1_out, and_2_out, and_3_out, and_4_out,
       and_5_out, and_6_out, and_7_out, and_8_out, and_9_out, or_1_out, or_2_out, or_3_out;

  _1_Bit_Comparator _1_Bit_Comparator (
    .A(A3), .B(B3), .E__A___B(_1_Bit_Comparator_e__a___b), .S__A___B(_1_Bit_Comparator_s__a___b));
  _1_Bit_Comparator _1_Bit_Comparator_2 (
    .A(A2), .B(B2), .E__A___B(_1_Bit_Comparator_2_e__a___b), .S__A___B(_1_Bit_Comparator_2_s__a___b));
  _1_Bit_Comparator _1_Bit_Comparator_3 (
    .A(A1), .B(B1), .E__A___B(_1_Bit_Comparator_3_e__a___b), .S__A___B(_1_Bit_Comparator_3_s__a___b));
  _1_Bit_Comparator _1_Bit_Comparator_4 (
    .A(Ao), .B(Bo), .E__A___B(_1_Bit_Comparator_4_e__a___b), .S__A___B(_1_Bit_Comparator_4_s__a___b));
  and and_1 (and_1_out, _1_Bit_Comparator_e__a___b, _1_Bit_Comparator_2_e__a___b);
  and and_2 (and_2_out, _1_Bit_Comparator_e__a___b, _1_Bit_Comparator_2_e__a___b);
  and and_3 (and_3_out, _1_Bit_Comparator_3_e__a___b, _1_Bit_Comparator_4_s__a___b);
  and and_4 (and_4_out, _1_Bit_Comparator_e__a___b, _1_Bit_Comparator_2_e__a___b);
  and and_5 (and_5_out, _1_Bit_Comparator_3_e__a___b, _1_Bit_Comparator_4_e__a___b);
  and and_6 (and_6_out, and_1_out, _1_Bit_Comparator_3_s__a___b);
  and and_7 (and_7_out, and_2_out, and_3_out);
  and and_8 (and_8_out, and_4_out, and_5_out);
  and and_9 (and_9_out, _1_Bit_Comparator_e__a___b, _1_Bit_Comparator_2_s__a___b);
  or or_1 (or_1_out, _1_Bit_Comparator_s__a___b, and_9_out);
  or or_2 (or_2_out, and_6_out, and_7_out);
  or or_3 (or_3_out, or_1_out, or_2_out);
  or or_4 (A__B, or_3_out, and_8_out);
endmodule

// Sub
module _4_Bit_Subtractor (
  input  [3:0] A,
  input  [3:0] B,
  output [3:0] Result
);

  wire full_adder_1_carry, full_adder_2_carry, full_adder_3_carry, full_adder_4_carry, not_1_out, not_2_out,
       not_3_out, not_4_out;

  not not_1 (not_1_out, B[0]);
  not not_2 (not_2_out, B[1]);
  not not_3 (not_3_out, B[2]);
  not not_4 (not_4_out, B[3]);
  Full_Adder full_adder_1 (.x(A[0]), .y(not_1_out), .z(1'b1), .SUM(Result[0]), .CARRY(full_adder_1_carry));
  Full_Adder full_adder_2 (
    .x(A[1]), .y(not_2_out), .z(full_adder_1_carry), .SUM(Result[1]), .CARRY(full_adder_2_carry));
  Full_Adder full_adder_3 (
    .x(A[2]), .y(not_3_out), .z(full_adder_2_carry), .SUM(Result[2]), .CARRY(full_adder_3_carry));
  Full_Adder full_adder_4 (
    .x(A[3]), .y(not_4_out), .z(full_adder_3_carry), .SUM(Result[3]), .CARRY(full_adder_4_carry));
  // also tied to GND on the sheet: full_adder_4_carry
endmodule

module Q___B (
  input  Q,
  input  [3:0] B,
  output [3:0] Result
);

  and and_1 (Result[3], Q, B[3]);
  and and_2 (Result[2], B[2], Q);
  and and_3 (Result[1], B[1], Q);
  and and_4 (Result[0], B[0], Q);
endmodule

module Division (
  input  [4:0] A,
  input  [4:0] B,
  output [7:0] Result,
  output Div_by_Zero,
  output Sign
);

  wire not_2_out, not_3_out, not_4_out, or_1_out, or_2_out, or_3_out, or_4_out, or_5_out, or_6_out, or_7_out,
       or_8_out, or_9_out, or_10_out, xor_1_out;

  or or_1 (or_1_out, B[0], B[1]);
  or or_2 (or_2_out, or_1_out, B[2]);
  or or_3 (or_3_out, or_2_out, B[3]);
  not not_1 (Div_by_Zero, or_3_out);
  xor xor_1 (xor_1_out, A[4], B[4]);
  or or_4 (or_4_out, A[0], A[1]);
  or or_5 (or_5_out, or_4_out, A[2]);
  _4_Bit_Divider Divider (.A(A[3:0]), .B(B[3:0]), .Q1(Result[3]), .Q2(Result[2]), .Q3(Result[1]), .Q4(Result[0]));
  or or_6 (or_6_out, or_5_out, A[3]);
  not not_2 (not_2_out, or_6_out);
  or or_7 (or_7_out, B[0], B[1]);
  or or_8 (or_8_out, or_7_out, B[2]);
  not not_3 (not_3_out, or_9_out);
  or or_9 (or_9_out, or_8_out, B[3]);
  or or_10 (or_10_out, not_2_out, not_3_out);
  not not_4 (not_4_out, or_10_out);
  and and_1 (Sign, xor_1_out, not_4_out);

  assign Result[7:4] = 4'b0000;
endmodule
