// Logisim project Project.circ as structural Verilog: 4 circuits, main circuit main
module main (
  input  [1:0] Mode_of_Operation,
  input  [4:0] Input_1___A,
  input  [4:0] Input_2___B
);

  wire alu_1_div_by_zero, alu_1_sign, alu_1_zero, convert_to_bcd_1_out_2, convert_to_bcd_1_out_3,
       convert_to_bcd_1_out_4, convert_to_bcd_1_out_5, convert_to_bcd_1_out_6, convert_to_bcd_1_out_7,
       convert_to_bcd_1_out_8, convert_to_bcd_1_out_9, convert_to_bcd_1_out_10, convert_to_bcd_1_out_11,
       convert_to_bcd_1_out_12, convert_to_bcd_1_out_13, Hundreds_a, Hundreds_b, Hundreds_c, Hundreds_d,
       Hundreds_e, Hundreds_f, Hundreds_g, Tens_a, Tens_b, Tens_c, Tens_d, Tens_e, Tens_f, Tens_g, Units_a,
       Units_b, Units_c, Units_d, Units_e, Units_f, Units_g;
  wire [7:0] alu_1_out_4;

  LED Sign (.in(alu_1_sign));
  ALU alu_1 (
    .A(Input_1___A), .B(Input_2___B), .in_1(Mode_of_Operation), .Sign(alu_1_sign), .Zero(alu_1_zero),
    .Div_by_Zero(alu_1_div_by_zero), .out_4(alu_1_out_4));
  LED Zero (.in(alu_1_zero));
  LED Div_by_Zero (.in(alu_1_div_by_zero));
  Convert_To_BCD convert_to_bcd_1 (
    .in_1(alu_1_out_4), .out_2(convert_to_bcd_1_out_2), .out_3(convert_to_bcd_1_out_3),
    .out_4(convert_to_bcd_1_out_4), .out_5(convert_to_bcd_1_out_5), .out_6(convert_to_bcd_1_out_6),
    .out_7(convert_to_bcd_1_out_7), .out_8(convert_to_bcd_1_out_8), .out_9(convert_to_bcd_1_out_9),
    .out_10(convert_to_bcd_1_out_10), .out_11(convert_to_bcd_1_out_11), .out_12(convert_to_bcd_1_out_12),
    .out_13(convert_to_bcd_1_out_13));
  BCD_to_7Segments Units (
    ._1(convert_to_bcd_1_out_13), ._2(convert_to_bcd_1_out_12), ._3(convert_to_bcd_1_out_11),
    ._4(convert_to_bcd_1_out_10), .a(Units_a), .b(Units_b), .c(Units_c), .d(Units_d), .e(Units_e),
    .f(Units_f), .g(Units_g));
  BCD_to_7Segments Tens (
    ._1(convert_to_bcd_1_out_9), ._2(convert_to_bcd_1_out_8), ._3(convert_to_bcd_1_out_7),
    ._4(convert_to_bcd_1_out_6), .a(Tens_a), .b(Tens_b), .c(Tens_c), .d(Tens_d), .e(Tens_e), .f(Tens_f),
    .g(Tens_g));
  BCD_to_7Segments Hundreds (
    ._1(convert_to_bcd_1_out_5), ._2(convert_to_bcd_1_out_4), ._3(convert_to_bcd_1_out_3),
    ._4(convert_to_bcd_1_out_2), .a(Hundreds_a), .b(Hundreds_b), .c(Hundreds_c), .d(Hundreds_d),
    .e(Hundreds_e), .f(Hundreds_f), .g(Hundreds_g));
  _7_Segment_Display u_7_segment_display_1 (
    .g(Units_g), .f(Units_f), .a(Units_a), .b(Units_b), .e(Units_e), .d(Units_d), .c(Units_c));  // open: dp
  _7_Segment_Display u_7_segment_display_2 (
    .g(Tens_g), .f(Tens_f), .a(Tens_a), .b(Tens_b), .e(Tens_e), .d(Tens_d), .c(Tens_c));  // open: dp
  _7_Segment_Display u_7_segment_display_3 (
    .g(Hundreds_g), .f(Hundreds_f), .a(Hundreds_a), .b(Hundreds_b), .e(Hundreds_e), .d(Hundreds_d),
    .c(Hundreds_c));  // open: dp

  // Notes on the sheet:
  //   00 ------> Addition
  //   01 ------> Subtraction
  //   10 ------> Multiplication
  //   11 ------> Division
endmodule

module ALU (
  input  [1:0] in_1,
  input  [4:0] A,
  input  [4:0] B,
  output [7:0] out_4,
  output Sign,
  output Zero,
  output Div_by_Zero
);

  wire Addition_sign, Division_div_by_zero, Division_sign, Multiplication_sign, or_1_out, or_2_out, or_3_out,
       or_4_out, or_5_out, or_6_out, or_7_out, Subtraction_sign;
  wire [7:0] Addition_summation, Division_result, Multiplication_result, Subtraction_subtraction;

  Addition Addition (.A(A), .B(B), .Summation(Addition_summation), .Sign(Addition_sign));
  Subtraction Subtraction (.InPut_A(A), .InPut_B(B), .Subtraction(Subtraction_subtraction), .Sign(Subtraction_sign));
  Multiplier Multiplication (.B(A), .A(B), .Result(Multiplication_result), .Sign(Multiplication_sign));
  Division Division (.A(A), .B(B), .Div_by_Zero(Division_div_by_zero), .Result(Division_result), .Sign(Division_sign));
  _8Bit_Multiplexer u_8bit_multiplexer_1 (
    .in_2(Addition_summation), .in_3(Subtraction_subtraction), .in_4(Multiplication_result),
    .in_5(Division_result), .in_6(Addition_sign), .in_7(Subtraction_sign), .in_8(Multiplication_sign),
    .in_9(Division_sign), .in_10(Division_div_by_zero), .in_1(in_1), .out_11(out_4), .Sign(Sign),
    .Div_By_Zero(Div_by_Zero));
  or or_1 (or_1_out, out_4[7], out_4[6]);
  or or_2 (or_2_out, or_1_out, out_4[5]);
  or or_3 (or_3_out, or_2_out, out_4[4]);
  or or_4 (or_4_out, or_3_out, out_4[3]);
  or or_5 (or_5_out, or_4_out, out_4[2]);
  or or_6 (or_6_out, or_5_out, out_4[1]);
  or or_7 (or_7_out, or_6_out, out_4[0]);
  not not_1 (Zero, or_7_out);
endmodule

module Multiplexer (
  input  A,
  input  B,
  input  C,
  input  D,
  input  b_2,
  input  a_2,
  output Q
);

  wire and_1_out, and_2_out, and_3_out, and_4_out, and_5_out, and_6_out, nand_1_out, nand_2_out, nand_3_out,
       nand_4_out, not_1_out, not_2_out;

  not not_1 (not_1_out, b_2);
  not not_2 (not_2_out, a_2);
  and and_1 (and_1_out, A, not_1_out);
  and and_2 (and_2_out, B, not_1_out);
  and and_3 (and_3_out, C, not_2_out);
  and and_4 (and_4_out, D, b_2);
  nand nand_1 (nand_1_out, and_1_out, not_2_out);
  nand nand_2 (nand_2_out, and_2_out, a_2);
  nand nand_3 (nand_3_out, and_3_out, b_2);
  nand nand_4 (nand_4_out, and_4_out, a_2);
  and and_5 (and_5_out, nand_1_out, nand_2_out);
  and and_6 (and_6_out, nand_3_out, nand_4_out);
  nand nand_5 (Q, and_5_out, and_6_out);
endmodule

module _8Bit_Multiplexer (
  input  [1:0] in_1,
  input  [7:0] in_2,
  input  [7:0] in_3,
  input  [7:0] in_4,
  input  [7:0] in_5,
  input  in_6,
  input  in_7,
  input  in_8,
  input  in_9,
  input  in_10,
  output [7:0] out_11,
  output Sign,
  output Div_By_Zero
);

  Multiplexer multiplexer_1 (
    .A(in_2[0]), .B(in_3[0]), .C(in_4[0]), .D(in_5[0]), .b_2(in_1[1]), .a_2(in_1[0]), .Q(out_11[0]));
  Multiplexer multiplexer_2 (
    .A(in_2[1]), .B(in_3[1]), .C(in_4[1]), .D(in_5[1]), .b_2(in_1[1]), .a_2(in_1[0]), .Q(out_11[1]));
  Multiplexer multiplexer_3 (
    .A(in_2[2]), .B(in_3[2]), .C(in_4[2]), .D(in_5[2]), .b_2(in_1[1]), .a_2(in_1[0]), .Q(out_11[2]));
  Multiplexer multiplexer_4 (
    .A(in_2[3]), .B(in_3[3]), .C(in_4[3]), .D(in_5[3]), .b_2(in_1[1]), .a_2(in_1[0]), .Q(out_11[3]));
  Multiplexer multiplexer_5 (
    .A(in_2[4]), .B(in_3[4]), .C(in_4[4]), .D(in_5[4]), .b_2(in_1[1]), .a_2(in_1[0]), .Q(out_11[4]));
  Multiplexer multiplexer_6 (
    .A(in_2[5]), .B(in_3[5]), .C(in_4[5]), .D(in_5[5]), .b_2(in_1[1]), .a_2(in_1[0]), .Q(out_11[5]));
  Multiplexer multiplexer_7 (
    .A(in_2[6]), .B(in_3[6]), .C(in_4[6]), .D(in_5[6]), .b_2(in_1[1]), .a_2(in_1[0]), .Q(out_11[6]));
  Multiplexer multiplexer_8 (
    .A(in_2[7]), .B(in_3[7]), .C(in_4[7]), .D(in_5[7]), .b_2(in_1[1]), .a_2(in_1[0]), .Q(out_11[7]));
  Multiplexer multiplexer_9 (.A(in_6), .B(in_7), .C(in_8), .D(in_9), .b_2(in_1[1]), .a_2(in_1[0]), .Q(Sign));
  Multiplexer multiplexer_10 (.A(1'b0), .B(1'b0), .C(1'b0), .D(in_10), .b_2(in_1[1]), .a_2(in_1[0]), .Q(Div_By_Zero));
endmodule
